// Logisim project Assessment-01.circ as structural Verilog: 1 circuit, main circuit main
module main (
  input  A,
  input  B,
  input  C,
  input  D,
  output F___A_B_C_D
);

  wire or_1_out, or_2_out;

  or or_1 (or_1_out, A, B);
  or or_2 (or_2_out, C, D);
  or or_3 (F___A_B_C_D, or_1_out, or_2_out);
endmodule
